// Logisim project Atividade do vídeo Circuitos Lógicos no LogiSim.circ as structural Verilog: 1 circuit, main circuit main
module main (
  input  A,
  input  in_2,
  input  B,
  input  in_4,
  input  C,
  input  A_2,
  input  D,
  input  B_2,
  input  in_9,
  input  A_3,
  input  in_11,
  input  B_3,
  input  C_2,
  input  D_2,
  input  B_4,
  input  C_3,
  input  E,
  input  A_4,
  input  D_3,
  input  E_2,
  output out_21,
  output out_22,
  output out_23,
  output out_24,
  output out_25
);

  wire and_2_out, and_3_out, and_4_out, and_6_out, and_7_out, and_8_out, or_1_out, or_2_out, or_4_out,
       or_5_out;

  and and_1 (out_21, in_2, in_4);
  and and_2 (and_2_out, A_2, B_2);
  and and_3 (and_3_out, in_9, in_11);
  or or_1 (or_1_out, B_4, C_3);
  and and_4 (and_4_out, or_1_out, or_2_out);
  or or_2 (or_2_out, D_3, E_2);
  or or_3 (out_23, and_2_out, and_3_out);
  and and_5 (out_25, and_4_out, A_4);
  and and_6 (and_6_out, A_3, B_3);
  and and_7 (and_7_out, A, B);
  or or_4 (or_4_out, and_6_out, C_2);
  or or_5 (or_5_out, and_7_out, C);
  and and_8 (and_8_out, or_4_out, D_2);
  and and_9 (out_22, or_5_out, D);
  or or_6 (out_24, and_8_out, E);

  // Notes on the sheet:
  //   Y = A .B 
  //   Y = (A .B) + (C . D)
  //   Y = A. (B+C) . (D + E)
  //   Y = A . B + C. D + E
  //   Y = A. B + C. D
endmodule
