// Logisim project trabalho arquitetura.circ as structural Verilog: 2 circuits, main circuit somador 1bit
module somador_1bit (
  input  A,
  input  B,
  input  vem_um,
  output vai_um,
  output soma
);

  wire and_1_out, and_2_out, and_3_out, and_4_out, and_5_out, and_6_out, and_7_out, not_1_out, not_2_out,
       not_3_out;

  not not_1 (not_1_out, A);
  not not_2 (not_2_out, vem_um);
  not not_3 (not_3_out, B);
  and and_1 (and_1_out, A, vem_um);
  and and_2 (and_2_out, A, B);
  and and_3 (and_3_out, B, vem_um);
  and and_4 (and_4_out, not_1_out, not_3_out, vem_um);
  and and_5 (and_5_out, not_1_out, B, not_2_out);
  and and_6 (and_6_out, A, not_3_out, not_2_out);
  and and_7 (and_7_out, A, B, vem_um);
  or or_1 (vai_um, and_1_out, and_2_out, and_3_out);
  or or_2 (soma, and_4_out, and_5_out, and_6_out, and_7_out);
endmodule

module main (
  input  in_1,
  input  in_2,
  input  in_3,
  input  in_4,
  input  in_5,
  input  in_6,
  input  in_7,
  input  in_8,
  input  in_9,
  input  in_10,
  input  in_11,
  input  in_12,
  input  in_13,
  input  in_14,
  input  in_15,
  input  in_16,
  input  in_17,
  input  in_18,
  output out_19,
  output out_20,
  output out_21,
  output out_22,
  output out_23,
  output out_24,
  output out_25,
  output out_26,
  output out_27,
  output out_28
);

  wire _0bit_soma, _1bit_soma, _2bit_soma, _3bit_soma, _4bit_soma, _5bit_soma, _6bit_soma, _7bit_soma;

  somador_1bit _0bit (.A(in_9), .B(in_18), .vem_um(1'b0), .vai_um(out_28), .soma(_0bit_soma));
  somador_1bit _1bit (.A(in_8), .B(in_17), .vem_um(_0bit_soma), .vai_um(out_27), .soma(_1bit_soma));
  somador_1bit _2bit (.A(in_7), .B(in_16), .vem_um(_1bit_soma), .vai_um(out_26), .soma(_2bit_soma));
  somador_1bit _3bit (.A(in_6), .B(in_15), .vem_um(_2bit_soma), .vai_um(out_25), .soma(_3bit_soma));
  somador_1bit _4bit (.A(in_5), .B(in_14), .vem_um(_3bit_soma), .vai_um(out_24), .soma(_4bit_soma));
  somador_1bit _5bit (.A(in_4), .B(in_13), .vem_um(_4bit_soma), .vai_um(out_23), .soma(_5bit_soma));
  somador_1bit _6bit (.A(in_3), .B(in_12), .vem_um(_5bit_soma), .vai_um(out_22), .soma(_6bit_soma));
  somador_1bit _7bit (.A(in_2), .B(in_11), .vem_um(_6bit_soma), .vai_um(out_21), .soma(_7bit_soma));
  somador_1bit _8bit (.A(in_1), .B(in_10), .vem_um(_7bit_soma), .vai_um(out_20), .soma(out_19));
endmodule
